# Fritzing sketch logger (saved by Fritzing 0.9.2b)

parts:
  LIS3DH1 = LIS3DH Accelerometer Breakout  # not connected
  proto1 = Adafruit Feather Wing Proto

nets:
  N1: proto1.connector36, proto1.connector72
  N2: proto1.connector43, proto1.connector88
  N3: proto1.connector97, proto1.connector139
  N4: proto1.connector106, proto1.connector148

custom parts:
  LIS3DH Accelerometer Breakout: LIS3DH Accelerometer Breakout board
